# Fritzing sketch fritzing (saved by Fritzing 0.9.10b)
breadboards: 1

parts:
  Part1 = Feather S2
  Part2 = Adafruit 2.9in eInk Under FeatherWing
  Water_Temp = DS18B20 1-Wire Temperature Sensor [part_number=DS18B20]
  R1 = Resistor [tolerance=±5% resistance=220 package="0603 [SMD]"]
  pH = TMP36 [package=to-92]
  DO = TMP36 [package=to-92]
  Q6 = MOSFET-NCHANNEL [package=to220v]
  Q7 = MOSFET-NCHANNEL [package=to220v]
  U1 = LIPO-2000mAh [package=lipo-2000]
  Part3 = Adafruit BQ24074 Solar-DC-USB Lipo Charger
  R2 = Temperature Sensor (Thermistor) [thermistor_type=NTC package=THT]
  R5 = Resistor [tolerance=±5% resistance=220 package="1206 [SMD]"]
  R6 = Resistor [tolerance=±5% resistance=220 package="1206 [SMD]"]

nets:
  N1: Part1.RESET, Part2.RESET
  3V3: Part1.3V3, Part2.3.3V
  N2: Part1.IO0, Part2.AREF
  GND: Part1.GND, Part2.GND, Water_Temp.GND, Q6.S, Q7.S, U1.-, Part3.GND, R2.pin_0
  N3: Part1.IO17_A0, Part2.A0
  N4: Part1.IO18_A1, Part2.6, Part2.6B, Water_Temp.DQ, R1.Pin_0
  N5: Part1.IO14_A2, Part2.7, Part2.7B
  N6: Part1.IO12_A3, Part2.8, Part2.8B, R6.Pin_1
  N7: Part1.IO6_A4, Part2.9, Part2.9B, R5.Pin_1
  N8: Part1.IO5_A5, Part2.10, Part2.10B
  N9: Part1.SCK, Part2.SCLK
  N10: Part1.SDO, Part2.MOSI
  N11: Part1.SDI, Part2.MISO
  N12: Part1.RX, Part2.N$14, Part2.14B
  N13: Part1.TX, Part2.N$15, Part2.15B
  N14: Part1.3V3_2, Part2.N$16, Part2.16B
  N15: Part1.VBAT, Part2.VBAT
  N16: Part1.EN, Part2.EN, Part3.OUT
  N17: Part1.USB, Part2.USB
  N18: Part1.IO11_A6, Part2.25, Part2.25B
  N19: Part1.IO10_A7, Part2.24, Part2.24B
  N20: Part1.IO7_A8, Part2.23, Part2.23B
  N21: Part1.IO3_A9, Part2.K
  N22: Part1.IO1_A10, Part2.J
  N23: Part1.IO38, Part2.I
  N24: Part1.IO33, Part2.H
  N25: Part1.SCL, Part2.N$18, Part2.18B
  N26: Part1.SDA, Part2.N$17, Part2.17B
  N27: Water_Temp.VDD, R1.Pin_1
  N28: pH.GND, Q7.D
  N29: DO.GND, Q6.D
  N30: Q6.G, R5.Pin_0
  N31: Q7.G, R6.Pin_0
  N32: U1.+, Part3.VLIPO
  N33: Part3.THERM, R2.pin_1

custom parts:
  Feather S2: The Feather S2 uses the new ESP32-S2 micro-controller from Espressif. It's one of their new generation of Sx MCUs that has the newer Xtensa LX7 core running at 240MHz, a RISC-V ultra low power co-processor, WiFi and built in USB. It has 16 MB of flash and 8MB of SPI based external RAM.
